# Fritzing sketch schematic (saved by Fritzing 0.9.3b)
breadboards: 1

parts:
  Raspberry_Pi1 = Raspberry Pi 2
  hc-sr1 = hc-sr04
  LED1 = smd LED [color="Red (633nm)" package="0603 [SMD]"]
  R1 = Resistor [tolerance=±5% resistance=220 package=THT]

nets:
  5V: Raspberry_Pi1.GPIO2, Raspberry_Pi1.5V, hc-sr1.VCC
  N1: Raspberry_Pi1.GPIO18, LED1.anode
  N2: Raspberry_Pi1.GPIO15, hc-sr1.Trig
  N3: Raspberry_Pi1.GPIO14, hc-sr1.Echo
  GND: Raspberry_Pi1.GND, hc-sr1.GND, R1.Pin_0
  N4: LED1.cathode, R1.Pin_1
